# Fritzing sketch UPS_Control (saved by Fritzing 0.9.4)

parts:
  WeMos_D1_Mini1 = WeMos D1 Mini
  Компонент1 = MAX3232
  HLK-PM1 = HLK-PM03
  X1 = DB9 Connector [package=db9]
  X2 = DB9 Connector [package=db9]

nets:
  3V3: WeMos_D1_Mini1.3V3, Компонент1.VCC, HLK-PM1.-Vo
  N1: WeMos_D1_Mini1.D1, Компонент1.RXD
  N2: WeMos_D1_Mini1.D2, Компонент1.TXD
  N3: WeMos_D1_Mini1.G, Компонент1.GND, HLK-PM1.+Vo
  N4: X1.5, X2.5
  N5: X1.7, X2.8
  N6: X1.8, X2.7

custom parts:
  MAX3232: A random MAX3232 Breakout Board from AliExpress (RS232-TTL-Converter)
  HLK-PM03: AC-DC 220V to 3.3V Step-Down Power Supply Module
